// Logisim project DES_project.circ as structural Verilog: 3 circuits, main circuit main
module main (
  input  [2:0] in_1,
  output [3:0] out_2
);

  wire clock_1_out;
  wire [5:0] bitselector_1_out;
  wire [31:0] random_1_out;
  wire [47:0] e_box_1_ex_output;

  Clock clock_1 (.out(clock_1_out));
  Random #(.width(32)) random_1 (.clk(clock_1_out), .out(random_1_out));  // open: clr, next
  E_box e_box_1 (.ex_input(random_1_out), .ex_output(e_box_1_ex_output));
  // Probe on bitselector_1_out
  BitSelector #(.group(6), .width(48)) bitselector_1 (.in(e_box_1_ex_output), .out(bitselector_1_out), .sel(in_1));
  S_box_1 s_box_1_1 (.sb_1_input(bitselector_1_out), .sb_1_output(out_2));
endmodule

module S_box_1 (
  input  [5:0] sb_1_input,
  output [3:0] sb_1_output
);

  ROM #(.addrWidth(6), .dataWidth(4)) rom_1 (.addr(sb_1_input), .data(sb_1_output));

  // Notes on the sheet:
  //   contents of rom_1 (hex, n*v repeats v):
  //   e 0 4 f d 7 1 4 2 e f 2 b d 8 1 3 a a 6 6 c c b 5 9 9 5 0 3 7 8 4 f 1 c e 8 8 2 d 4 6 9 2 1 b 7 f 5
  //   c b 9 3 7 e 3 a a 0 5 6 0 d
endmodule

module E_box (
  input  [31:0] ex_input,
  output [47:0] ex_output
);


  assign ex_output = {ex_input[0], ex_input[31:27], ex_input[28:23], ex_input[24:19], ex_input[20:15], ex_input[16:11], ex_input[12:7], ex_input[8:3], ex_input[4:0], ex_input[31]};
endmodule
